# Fritzing sketch Ampel (saved by Fritzing 0.9.10b)
circuit board: 1.5cm x 3.46cm
breadboards: 1

parts:
  LED1 = LED - 5mm [color="Red (633nm)" current=0.030 package="5 mm [THT]"]
  LED2 = LED - 5mm [color="Red (633nm)" current=0.030 package="5 mm [THT]"]
  LED3 = LED - 5mm [color="Red (633nm)" current=0.030 package="5 mm [THT]"]
  R1 = Resistor [tolerance=±5% power=0.25 resistance=220 package=THT]
  J1 = female pin header, 4 pins [form="♀ (female)"]

nets:
  N1: LED1.cathode, LED2.cathode, LED3.cathode, R1.Pin_0
  N2: LED1.anode, J1.pin3
  N3: LED2.anode, J1.pin2
  N4: LED3.anode, J1.pin1
  N5: R1.Pin_1, J1.pin4

notes:
  - R G G
  Gymnasium Waldkraiburg
  Wahlkurs Mikroelektronik
