# Fritzing sketch ArduShield1-1 (saved by Fritzing 0.9.10b)
circuit board: 4.07652cm x 5.32022cm
breadboards: 1

parts:
  J2 = female pin header, 6 pins [form="♀ (female)"]
  J4 = female pin header, 6 pins [form="♀ (female)"]
  J6 = female pin header, 6 pins [form="♀ (female)"]
  J1 = female pin header, 6 pins [form="♀ (female)"]
  J7 = female pin header, 6 pins [form="♀ (female)"]
  J3 = female pin header, 6 pins [form="♀ (female)"]
  J9 = female pin header, 6 pins [form="♀ (female)"]
  J5 = female pin header, 6 pins [form="♀ (female)"]
  J10 = female pin header, 6 pins [form="♀ (female)"]
  Bauteil1 = Arduino Uno (Rev3)
  J8 = female pin header, 4 pins [form="♀ (female)"]
  J11 = female pin header, 2 pins [form="♀ (female)"]

nets:
  N1: J2.pin1, Bauteil1.A5/SCL
  N2: J2.pin2, Bauteil1.A4/SDA
  N3: J2.pin3, Bauteil1.A3
  N4: J2.pin4, Bauteil1.A2
  N5: J2.pin5, Bauteil1.A1
  N6: J2.pin6, Bauteil1.A0
  N7: J4.pin1, J4.pin2, J4.pin3, J4.pin4, J4.pin5, J4.pin6, J3.pin1, J3.pin2, J3.pin3, J3.pin4, J3.pin5, J3.pin6, J9.pin1, J9.pin2, J9.pin3, J9.pin4, J9.pin5, J9.pin6, Bauteil1.GND
  N8: J6.pin1, J6.pin2, J6.pin3, J6.pin4, J6.pin5, J6.pin6, J5.pin1, J5.pin2, J5.pin3, J5.pin4, J5.pin5, J5.pin6, J10.pin1, J10.pin2, J10.pin3, J10.pin4, J10.pin5, J10.pin6, Bauteil1.5V
  N9: J1.pin1, Bauteil1.D2
  N10: J1.pin2, Bauteil1.D3_PWM
  N11: J1.pin3, Bauteil1.D4
  N12: J1.pin4, Bauteil1.D5_PWM
  N13: J1.pin5, Bauteil1.D6_PWM
  N14: J1.pin6, Bauteil1.D7
  N15: J7.pin1, Bauteil1.D8
  N16: J7.pin2, Bauteil1.D9_PWM
  N17: J7.pin3, Bauteil1.D10_PWM/SS
  N18: J7.pin4, Bauteil1.D11_PWM/MOSI
  N19: J7.pin5, Bauteil1.D12/MISO
  N20: J7.pin6, Bauteil1.D13/SCK
  N21: Bauteil1.D0/RX, J11.pin1
  N22: Bauteil1.D1/TX, J11.pin2
  N23: Bauteil1.3V3, J8.pin1, J8.pin2, J8.pin3, J8.pin4

notes:
  5V
  GND
  3.3V
  Ardu-Shield 1.1
  Gymnasium Waldkraiburg
  07/2025  Rainer Hille
