# Fritzing sketch Motor1 (saved by Fritzing 0.9.6b)

parts:
  A1 = Adafruit v1.2 motor shield
  M1 = gear-motor
  M2 = gear-motor
  BAT1 = Battery Holders [package=battery-aa]

nets:
  N1: A1.Pin_6, BAT1.+
  N2: A1.Pin_7, A1.Pin_37, BAT1.-
  N3: A1.Pin_44, M1.pin_1
  N4: A1.Pin_45, M1.pin_2
  N5: A1.Pin_47, M2.pin_1
  N6: A1.Pin_48, M2.pin_2

custom parts:
  Adafruit v1.2 motor shield: Adafruit v1.2 motor shield.
