# Fritzing sketch Alarmanlage (saved by Fritzing 0.9.6b)
circuit board: 6.87357cm x 5.31284cm
breadboards: 1

parts:
  Bauteil1 = Arduino Uno (Rev3)
  J1 = female pin header, 3 pins [form="♀ (female)"]
  J2 = female pin header, 3 pins [form="♀ (female)"]
  R1 = Resistor [tolerance=±5% power=0.25 resistance=220 package=THT]
  J4 = female pin header, 3 pins [form="♀ (female)"]
  J3 = female pin header, 4 pins [form="♀ (female)"]

nets:
  N1: Bauteil1.D8, J2.pin3
  N2: Bauteil1.GND, J1.pin1, J4.pin3, J3.pin4
  N3: Bauteil1.D3_PWM, J4.pin1
  N4: Bauteil1.D5_PWM, J3.pin1
  N5: Bauteil1.D6_PWM, J1.pin2
  N6: Bauteil1.D7, J2.pin1
  N7: Bauteil1.5V, J1.pin3, R1.Pin_1, J4.pin2
  N8: J2.pin2, R1.Pin_0

notes:
  Bewegungsmelder
  +D-
  LED
  Buzzer
  -   A
  IR-FB
  -+D
  2024
  Wahlkurs Mikroelektronik
  Gymnasium Waldkraiburg
  Alarmanlage
  1 K
