# Fritzing sketch BatterieScrufe (saved by Fritzing 0.9.10b)
circuit board: 2.7413cm x 2.29737cm
breadboards: 1

parts:
  J1 = screw terminal, 2 pins
  J2 = screw terminal, 2 pins
  J3 = screw terminal, 2 pins

nets:
  N1: J1.pin1, J2.pin2
  N2: J1.pin2, J3.pin1
  N3: J2.pin1, J3.pin2

notes:
  +  -
  B1
  B2
  Ex
  +       -
