# Fritzing sketch 2FarbLED (saved by Fritzing 0.9.6b)
circuit board: 0.907564cm x 1.3443cm
breadboards: 1

parts:
  LED1 = DUO LED RG [package="5 mm [THT]"]
  J1 = female pin header, 3 pins [form="♀ (female)"]

nets:
  N1: LED1.red_anode, J1.pin3
  N2: LED1.common_cathode, J1.pin2
  N3: LED1.green_anode, J1.pin1

notes:
  R + G
