# Fritzing sketch LED (saved by Fritzing 0.9.10b)
circuit board: 1.12cm x 1.11747cm
breadboards: 1

parts:
  LED1 = LED - 5mm [color="Red (633nm)" current=0.030 package="5 mm [THT]"]
  J1 = female pin header, 2 pins [form="♀ (female)"]

nets:
  N1: LED1.cathode, J1.pin1
  N2: LED1.anode, J1.pin2

notes:
  +  -
