# Fritzing sketch ProtoShield (saved by Fritzing 0.9.6b)
circuit board: 6.61968cm x 5.30927cm
breadboards: 1

parts:
  J20 = female pin header, 20 pins [form="♀ (female)"]  # not connected
  J17 = female pin header, 16 pins [form="♀ (female)"]
  J18 = female pin header, 16 pins [form="♀ (female)"]
  J16 = female pin header, 16 pins [form="♀ (female)"]
  J14 = female pin header, 16 pins [form="♀ (female)"]
  J15 = female pin header, 16 pins [form="♀ (female)"]
  J12 = female pin header, 16 pins [form="♀ (female)"]
  J13 = female pin header, 16 pins [form="♀ (female)"]
  J11 = female pin header, 16 pins [form="♀ (female)"]
  J8 = female pin header, 12 pins [form="♀ (female)"]
  J6 = female pin header, 16 pins [form="♀ (female)"]
  J5 = female pin header, 16 pins [form="♀ (female)"]
  J4 = female pin header, 4 pins [form="♀ (female)"]
  J3 = female pin header, 18 pins [form="♀ (female)"]
  J1 = female pin header, 18 pins [form="♀ (female)"]
  J2 = female pin header, 18 pins [form="♀ (female)"]
  J34 = female pin header, 4 pins [form="♀ (female)"]
  Bauteil1 = Arduino Uno (Rev3)
  J7 = female pin header, 12 pins [form="♀ (female)"]  # not connected
  J9 = female pin header, 12 pins [form="♀ (female)"]
  J10 = female pin header, 12 pins [form="♀ (female)"]
  J35 = female pin header, 4 pins [form="♀ (female)"]
  J36 = double row female pin header, 8 pins [form="♀ (female)"]
  J25 = female pin header, 12 pins [form="♀ (female)"]  # not connected
  J37 = female pin header, 12 pins [form="♀ (female)"]  # not connected
  J38 = female pin header, 12 pins [form="♀ (female)"]  # not connected
  J39 = female pin header, 12 pins [form="♀ (female)"]  # not connected
  J21 = female pin header, 20 pins [form="♀ (female)"]  # not connected
  J30 = female pin header, 3 pins [form="♀ (female)"]  # not connected
  J31 = female pin header, 3 pins [form="♀ (female)"]  # not connected
  J32 = female pin header, 3 pins [form="♀ (female)"]  # not connected
  J29 = female pin header, 3 pins [form="♀ (female)"]  # not connected
  J19 = female pin header, 16 pins [form="♀ (female)"]
  J33 = female pin header, 14 pins [form="♀ (female)"]  # not connected

nets:
  N1: J17.pin1, Bauteil1.D2
  N2: J17.pin16, Bauteil1.A3
  N3: J18.pin1, Bauteil1.D1/TX
  N4: J18.pin16, J2.pin1, Bauteil1.A4/SDA
  N5: J16.pin1, Bauteil1.D3_PWM
  N6: J16.pin16, Bauteil1.A2
  N7: J14.pin1, Bauteil1.D5_PWM
  N8: J14.pin16, Bauteil1.A0
  N9: J15.pin1, Bauteil1.D4
  N10: J15.pin16, Bauteil1.A1
  N11: J12.pin1, Bauteil1.D7
  N12: J12.pin16, Bauteil1.VIN
  N13: J13.pin1, Bauteil1.D6_PWM
  N14: J11.pin1, Bauteil1.D11_PWM/MOSI
  N15: J11.pin16, Bauteil1.RESET
  N16: J8.pin1, Bauteil1.D10_PWM/SS
  N17: J6.pin1, Bauteil1.D12/MISO
  N18: J6.pin16, Bauteil1.ioref
  N19: J5.pin1, Bauteil1.D13/SCK
  N20: J5.pin16, Bauteil1.N/C
  N21: J4.pin1, J4.pin2, J4.pin3, J4.pin4, Bauteil1.GND, J36.pin1, J36.pin2, J36.pin3, J36.pin4, J36.pin5, J36.pin6, J36.pin7, J36.pin8
  N22: J3.pin1, Bauteil1.AREF
  N23: J1.pin1, Bauteil1.A5/SCL, J19.pin16
  N24: J34.pin1, J34.pin2, J34.pin3, J34.pin4, Bauteil1.3V3
  N25: Bauteil1.D8, J10.pin1
  N26: Bauteil1.D9_PWM, J9.pin1
  N27: Bauteil1.D0/RX, J19.pin1
  N28: Bauteil1.5V, J35.pin1, J35.pin2, J35.pin3, J35.pin4

notes:
  ProtoShield
  Gymnasium
  Wald-
  1.0
  kraiburg
