# Fritzing sketch RGBLED (saved by Fritzing 0.9.6b)
circuit board: 1.19994cm x 1.38709cm
breadboards: 1

parts:
  J1 = female pin header, 4 pins [form="♀ (female)"]
  LED1 = RGB LED (com. cathode, rgb) [package="5 mm [THT]"]

nets:
  N1: J1.pin1, LED1.blue_anode
  N2: J1.pin2, LED1.green_anode
  N3: J1.pin3, LED1.common_cathode
  N4: J1.pin4, LED1.red_anode

notes:
  R + G B
