# Fritzing sketch Taster (saved by Fritzing 0.9.10b)
circuit board: 1cm x 1.6cm
breadboards: 1

parts:
  S1 = Pushbutton [package="[THT]"]
  J1 = female pin header, 2 pins [form="♀ (female)"]
  J2 = female pin header, 2 pins [form="♀ (female)"]

nets:
  N1: S1.Pin_1, S1.Pin_2, J1.pin1, J1.pin2
  N2: S1.Pin_3, S1.Pin_4, J2.pin1, J2.pin2
