# Fritzing sketch Taster (saved by Fritzing 0.9.6b)
circuit board: 1.02166cm x 1.42275cm
breadboards: 1

parts:
  S1 = Pushbutton [package="[THT]"]
  J1 = female pin header, 3 pins [form="♀ (female)"]

nets:
  N1: S1.Pin_1, S1.Pin_2, J1.pin3
  N2: S1.Pin_3, J1.pin1, J1.pin2

notes:
  D R
