# Fritzing sketch Verbinder (saved by Fritzing 0.9.10b)
circuit board: 0.635cm x 1.08705cm
breadboards: 1

parts:
  J2 = male pin header, 4 pins [form="♂ (male)"]
  J1 = male pin header, 4 pins [form="♂ (male)"]

nets:
  N1: J2.pin1, J2.pin2, J2.pin3, J2.pin4, J1.pin1, J1.pin2, J1.pin3, J1.pin4
