# Fritzing sketch Verbinder (saved by Fritzing 0.9.6b)
circuit board: 0.4cm x 2cm
breadboards: 1

parts:
  J1 = female pin header, 7 pins [form="♀ (female)"]

nets:
  N1: J1.pin1, J1.pin2, J1.pin3, J1.pin4, J1.pin5, J1.pin6, J1.pin7
