# Fritzing sketch Widerstand (saved by Fritzing 0.9.10b)
circuit board: 1.5cm x 0.9cm
breadboards: 1

parts:
  R1 = Resistor [tolerance=±5% power=0.25 resistance=1k package=THT]
  J1 = female pin header, 2 pins [form="♀ (female)"]

nets:
  N1: R1.Pin_0, J1.pin2
  N2: R1.Pin_1, J1.pin1
