# Fritzing sketch SchaltungKugelbahn (saved by Fritzing 0.9.6b)

parts:
  L298N1 = L298N DC motor driver
  Bauteil1 = Arduino Uno (Rev3)
  Power_plug1 = Power plug
  M1 = gear-motor
  S1 = Pushbutton [package="[THT]"]

nets:
  N1: L298N1.OUT1, M1.pin_2
  N2: L298N1.OUT2, M1.pin_1
  12V: L298N1.12V, Power_plug1.VCC
  GND: L298N1.GND, Bauteil1.GND, Power_plug1.GND, S1.Pin_3, S1.Pin_4
  5V: L298N1.5V, Bauteil1.VIN
  N3: L298N1.ENA, Bauteil1.D10_PWM/SS
  N4: L298N1.IN1, Bauteil1.D9_PWM
  N5: L298N1.IN2, Bauteil1.D8
  N6: Bauteil1.D7, S1.Pin_1, S1.Pin_2

notes:
  +5 V für Arduino
  Motor Geschwindigkeit
  Netzteil
  Motor  Richtung
  Taster
  Motor Anschluss
  +7 V max. für Motor

custom parts:
  L298N DC motor driver: 2x DC motor driver with 78M05 positive voltage regulator (7..35 V) L298N: max 46 V, 2 A Set 5 V Enable jumper to enable 5 V regultor (needed for the L298N) and +5 V output at screw terminal or supply external +5 V at screw terminal Set ENA and/or ENB to +5 V to enable motor permanently or supply ENA and/or ENB with PWM signal IN1 and IN2 set rotation directory for motor A (OUT1/OUT2) IN2 and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
