# Fritzing sketch Display (saved by Fritzing 0.9.6b)
circuit board: 5.93288cm x 3.93445cm
breadboards: 1

parts:
  J5 = female pin header, 19 pins [form="♀ (female)"]
  J6 = female pin header, 19 pins [form="♀ (female)"]
  J3 = female pin header, 8 pins [form="♀ (female)"]
  J7 = female pin header, 1 pin [form="♀ (female)"]
  J8 = female pin header, 1 pin [form="♀ (female)"]
  J10 = female pin header, 1 pin [form="♀ (female)"]
  J11 = female pin header, 1 pin [form="♀ (female)"]
  J12 = female pin header, 1 pin [form="♀ (female)"]  # not connected
  J9 = female pin header, 12 pins [form="♀ (female)"]
  J13 = female pin header, 1 pin [form="♀ (female)"]  # not connected

nets:
  N1: J5.pin5, J3.pin3
  N2: J5.pin7, J3.pin4
  N3: J5.pin8, J3.pin2
  N4: J5.pin9, J8.pin1
  N5: J5.pin19, J3.pin1, J10.pin1
  N6: J6.pin4, J3.pin6
  N7: J6.pin9, J9.pin1
  N8: J6.pin10, J9.pin2
  N9: J6.pin11, J9.pin3
  N10: J6.pin12, J9.pin4
  N11: J6.pin13, J9.pin5
  N12: J6.pin14, J9.pin6
  N13: J6.pin15, J9.pin7
  N14: J6.pin16, J9.pin8
  N15: J6.pin17, J9.pin9
  N16: J6.pin18, J9.pin10
  N17: J6.pin19, J3.pin7, J9.pin11
  N18: J3.pin5, J7.pin1
  N19: J3.pin8, J11.pin1, J9.pin12

notes:
  USB
  5V
  LED
  VCC
  GND
  CS
  RES
  A0
  SDA
  SCK
  3V3
  15
