# Fritzing sketch DisplayESPFraese (saved by Fritzing 0.9.6b)
circuit board: 6.2807cm x 2.99604cm
breadboards: 1

parts:
  J5 = female pin header, 19 pins [form="♀ (female)"]
  J6 = female pin header, 19 pins [form="♀ (female)"]
  J3 = female pin header, 8 pins [form="♀ (female)"]
  J7 = female pin header, 1 pin [form="♀ (female)"]
  J8 = female pin header, 1 pin [form="♀ (female)"]
  J9 = female pin header, 1 pin [form="♀ (female)"]
  J10 = female pin header, 1 pin [form="♀ (female)"]

nets:
  N1: J5.pin5, J3.pin3
  N2: J5.pin7, J10.pin1
  N3: J5.pin8, J3.pin2
  N4: J5.pin9, J7.pin1
  N5: J5.pin19, J3.pin1, J3.pin8
  N6: J6.pin4, J3.pin6
  N7: J6.pin19, J3.pin7
  N8: J3.pin4, J9.pin1
  N9: J3.pin5, J8.pin1

notes:
  15
  13
  12
  14
  27
  CS
  SDA
  A0
  VCC
  RES
  LED
  GND
  SCK
  USB
