# Fritzing sketch DisplayPCB (saved by Fritzing 0.9.6b)
circuit board: 5.84734cm x 4.57349cm
breadboards: 1

parts:
  J5 = female pin header, 19 pins [form="♀ (female)"]
  J6 = female pin header, 19 pins [form="♀ (female)"]
  J3 = female pin header, 8 pins [form="♀ (female)"]
  J9 = female pin header, 22 pins [form="♀ (female)"]
  J10 = female pin header, 22 pins [form="♀ (female)"]

nets:
  N1: J5.pin1, J10.pin1
  N2: J5.pin2, J10.pin2
  N3: J5.pin3, J10.pin3
  N4: J5.pin4, J10.pin4
  N5: J5.pin5, J3.pin3
  N6: J5.pin6, J10.pin5, J10.pin6, J10.pin7, J10.pin8, J10.pin9
  N7: J5.pin7, J3.pin4
  N8: J5.pin8, J3.pin2
  N9: J5.pin9, J3.pin5
  N10: J5.pin10, J10.pin10
  N11: J5.pin11, J10.pin11
  N12: J5.pin12, J10.pin12
  N13: J5.pin13, J10.pin13
  N14: J5.pin14, J10.pin14
  N15: J5.pin15, J10.pin15
  N16: J5.pin16, J10.pin16
  N17: J5.pin17, J10.pin17
  N18: J5.pin18, J10.pin18
  N19: J5.pin19, J3.pin1, J3.pin8, J9.pin21, J9.pin22, J10.pin19, J10.pin20, J10.pin21, J10.pin22
  N20: J6.pin1, J9.pin1
  N21: J6.pin2, J9.pin2
  N22: J6.pin3, J9.pin3
  N23: J6.pin4, J3.pin6
  N24: J6.pin5, J9.pin5
  N25: J6.pin6, J9.pin6
  N26: J6.pin7, J9.pin7
  N27: J6.pin8, J9.pin8
  N28: J6.pin9, J9.pin9
  N29: J6.pin10, J9.pin10
  N30: J6.pin11, J9.pin11
  N31: J6.pin12, J9.pin12
  N32: J6.pin13, J9.pin13
  N33: J6.pin14, J9.pin14
  N34: J6.pin15, J9.pin15
  N35: J6.pin16, J9.pin16
  N36: J6.pin17, J9.pin17
  N37: J6.pin18, J9.pin18
  N38: J6.pin19, J3.pin7, J9.pin19, J9.pin20

notes:
  USB
  5V
  LED
  VCC
  GND
  CS
  RES
  A0
  SDA
  SCK
  3V3
  15
  EN
  SP
  SN
  34
  35
  32
  33
  25
  26
  2
  3
  CMD
  23
  22
  TX
  RX
  21
  19
  18
  CLK
  SD0
  SD1
  0
  4
  16
  17
  5
  ESP32 - 1,8-Zoll Display Shield
  Wahlkurs Mikroelektronik
  Gymnasium Waldkraiburg
  13
  12
  14
  27
